# Fritzing sketch MID (saved by Fritzing 0.9.3b)
breadboards: 3

parts:
  Part1 = Arduino Uno (Rev3) - ICSP
  Part2 = Thumb Joystick
  Part3 = Thumb Joystick
  Part4 = Analog Digital MUX Breakout
  S1 = Pushbutton [package="[THT]"]
  R1 = Resistor [tolerance=±5% resistance=220 package=THT]
  S2 = Pushbutton [package="[THT]"]
  R2 = Resistor [tolerance=±5% resistance=220 package=THT]
  S3 = Pushbutton [package="[THT]"]
  R3 = Resistor [tolerance=±5% resistance=220 package=THT]
  S4 = Pushbutton [package="[THT]"]
  R4 = Resistor [tolerance=±5% resistance=220 package=THT]
  S5 = Pushbutton [package="[THT]"]
  R5 = Resistor [tolerance=±5% resistance=220 package=THT]
  S6 = Pushbutton [package="[THT]"]
  R6 = Resistor [tolerance=±5% resistance=220 package=THT]
  S7 = Pushbutton [package="[THT]"]
  R7 = Resistor [tolerance=±5% resistance=220 package=THT]
  S8 = Pushbutton [package="[THT]"]
  R8 = Resistor [tolerance=±5% resistance=220 package=THT]
  Part5 = NRF24L01+ Breakout Board
  C1 = Capacitor [package=cap-pth-5mm]
  R9 = Resistor [tolerance=±5% resistance=220 package=THT]
  R10 = Resistor [tolerance=±5% resistance=220 package=THT]
  R11 = Resistor [tolerance=±5% resistance=220 package=THT]
  R12 = Resistor [tolerance=±5% resistance=220 package=THT]
  R13 = Resistor [tolerance=±5% resistance=220 package=THT]
  D1 = LTE-302 [package=lte-302]
  D2 = LTE-302 [package=lte-302]
  D3 = LTE-302 [package=lte-302]
  D4 = LTE-302 [package=lte-302]
  D5 = LTE-302 [package=lte-302]

nets:
  N1: Part1.A0, Part4.SIG
  N2: Part1.ICSP_MISO, Part1.D12/MISO, Part5.MISO
  N3: Part1.D8, Part5.CE
  N4: Part1.D10_PWM/SS, Part5.CS
  N5: Part1.D11_PWM/MOSI, Part5.MOSI
  N6: Part1.D13/SCK, Part5.SCK
  N7: Part1.D2, Part4.S0
  N8: Part1.D3_PWM, Part4.S1
  N9: Part1.D4, Part4.S2
  N10: Part1.D5_PWM, Part4.S3
  N11: Part1.D6_PWM, Part4.EN
  3V3: Part1.3V3, Part5.VCC, C1.2
  VCC: Part1.5V, Part2.VCC, Part3.VCC, Part4.C4, Part4.VCC, S1.Pin_3, S1.Pin_4, S2.Pin_3, S2.Pin_4, S3.Pin_3, S3.Pin_4, S4.Pin_3, S4.Pin_4, S5.Pin_3, S5.Pin_4, S6.Pin_3, S6.Pin_4
  GND: Part1.GND, Part2.GND, Part3.GND, Part4.GND, R1.Pin_1, R2.Pin_1, R3.Pin_1, R4.Pin_1, R5.Pin_1, Part5.GND, C1.1, D1.C, D2.C, D3.C, D4.C, D5.C
  N12: Part2.HORZ, Part4.C0
  N13: Part3.HORZ, Part4.C1
  N14: Part4.C2, S1.Pin_1, S1.Pin_2, R1.Pin_0
  N15: Part4.C3, S2.Pin_1, S2.Pin_2, R2.Pin_0
  N16: Part4.C5, S4.Pin_1, S4.Pin_2, R4.Pin_0
  N17: Part4.C6, S5.Pin_1, S5.Pin_2, R5.Pin_0
  N18: Part4.C7, S6.Pin_1, S6.Pin_2, R6.Pin_0
  N19: Part4.C8, R11.Pin_1
  N20: Part4.C9, R12.Pin_1
  N21: Part4.C10, R10.Pin_1
  N22: Part4.C11, R9.Pin_1
  N23: Part4.C12, R13.Pin_1
  N24: Part4.C13, S7.Pin_1, S7.Pin_2, R7.Pin_0
  N25: Part4.C14, S8.Pin_1, S8.Pin_2, R8.Pin_0
  N26: S3.Pin_1, S3.Pin_2, R3.Pin_0
  N27: R6.Pin_1, R7.Pin_1, R8.Pin_1
  N28: S7.Pin_3, S7.Pin_4, S8.Pin_3, S8.Pin_4
  N29: R9.Pin_0, D4.A
  N30: R10.Pin_0, D3.A
  N31: R11.Pin_0, D2.A
  N32: R12.Pin_0, D1.A
  N33: R13.Pin_0, D5.A
