# Fritzing sketch MID (saved by Fritzing 0.9.3b)
circuit board: 8.46667cm x 5.64444cm
breadboards: 1

parts:
  Part1 = Arduino Uno (Rev3) - ICSP
  Part2 = Thumb Joystick
  Part3 = Thumb Joystick
  Part4 = Analog Digital MUX Breakout
  WeMos_D1_Mini1 = WeMos D1 Mini

nets:
  N1: Part1.A0, Part4.SIG
  N2: Part1.ICSP_MOSI, Part1.D11_PWM/MOSI, Part4.S1
  N3: Part1.D9_PWM, Part4.EN
  N4: Part1.D10_PWM/SS, Part4.S0
  N5: Part1.D12/MISO, Part4.S2
  N6: Part1.D13/SCK, Part4.S3
  N7: Part1.D0/RX, WeMos_D1_Mini1.TX
  N8: Part1.D1/TX, WeMos_D1_Mini1.RX
  GND: Part2.GND, Part3.GND, Part4.GND, WeMos_D1_Mini1.G
  N9: Part2.HORZ, Part4.C0
  VCC: Part2.VCC, Part3.VCC, Part4.VCC, WeMos_D1_Mini1.3V3
  N10: Part3.HORZ, Part4.C1
