# Fritzing sketch RobotProto (1) (saved by Fritzing 0.9.3b)
circuit board: 11.0792cm x 10.2859cm
breadboards: 1

parts:
  MD03A1 = Dual VNH2SP30 Motor Driver [part_number=MD03A]
  Part2 = NRF24L01+ Breakout Board
  DC_Mot_Enc5 = DC Motor with two-phase hall-encoder [part_number=VT-E-G25A-06-177E]
  Part1 = Arduino Mega 2560 (Rev3)
  J1 = Basic Servo
  DC_Mot_Enc6 = DC Motor with two-phase hall-encoder [part_number=VT-E-G25A-06-177E]
  DC_Mot_Enc7 = DC Motor with two-phase hall-encoder [part_number=VT-E-G25A-06-177E]
  J4 = female pin header, 4 pins [form="♀ (female)"]
  J8 = screw terminal, 2 pins
  DC_Mot_Enc8 = DC Motor with two-phase hall-encoder [part_number=VT-E-G25A-06-177E]
  DC_Mot_Enc9 = DC Motor with two-phase hall-encoder [part_number=VT-E-G25A-06-177E]
  MD03A2 = Dual VNH2SP30 Motor Driver [part_number=MD03A]
  IC3 = H-Bridge [package=THT]
  M1 = Stepper Motor - Bipolar
  DC_Mot_Enc10 = DC Motor with two-phase hall-encoder [part_number=VT-E-G25A-06-177E]
  U1 = GAS_SENSOR [package=mq-3]

nets:
  N1: MD03A1.1INa, Part1.D7_PWM
  N2: MD03A1.1INb, Part1.D9_PWM
  N3: MD03A1.PWM, Part1.D40
  GND: MD03A1.GND, Part2.GND, DC_Mot_Enc5.pin4, Part1.GND, J1.gnd, DC_Mot_Enc6.pin4, J4.pin3, J8.pin1, DC_Mot_Enc9.pin4, MD03A2.GND, IC3.GND1, IC3.GND2, IC3.GND3, IC3.GND4, U1.H2
  5V: MD03A1.+5V_(IN), DC_Mot_Enc5.pin5, Part1.5V, J1.vcc, DC_Mot_Enc6.pin5, J4.pin4, DC_Mot_Enc9.pin5, MD03A2.+5V_(IN), IC3.1_2EN, U1.H1
  N4: MD03A1.2PWM, Part1.D4_PWM
  N5: MD03A1.2INb#142, Part1.D5_PWM
  N6: MD03A1.2INb#143, Part1.D6_PWM
  N7: MD03A1.OUT_1A, DC_Mot_Enc6.pin1, DC_Mot_Enc8.pin1
  N8: MD03A1.OUT_1B, DC_Mot_Enc6.pin2, DC_Mot_Enc8.pin2
  N9: MD03A1.OUT_2A, DC_Mot_Enc7.pin1, DC_Mot_Enc9.pin1
  N10: MD03A1.OUT_2B, DC_Mot_Enc7.pin2, DC_Mot_Enc9.pin2
  VIN: MD03A1.VIN, Part1.VIN, J8.pin2, MD03A2.VIN, IC3.VCC1
  VCC: Part2.VCC, Part1.3V3
  N11: Part2.CE, Part1.D8_PWM
  N12: Part2.CS, Part1.D53
  N13: Part2.SCK, Part1.D52
  N14: Part2.MOSI, Part1.D51
  N15: Part2.MISO, Part1.D50
  N16: DC_Mot_Enc5.pin1, MD03A2.OUT_1A
  N17: DC_Mot_Enc5.pin2, MD03A2.OUT_1B
  N18: DC_Mot_Enc5.pin3, Part1.D2_PWM
  N19: DC_Mot_Enc5.pin6, Part1.D3_PWM
  N20: Part1.A0, J4.pin1, U1.B1
  N21: Part1.D21/SCL, DC_Mot_Enc9.pin6
  N22: Part1.D20/SDA, DC_Mot_Enc9.pin3
  N23: Part1.D19/RX1, DC_Mot_Enc6.pin6
  N24: Part1.D18/TX1, DC_Mot_Enc6.pin3
  N25: Part1.D22, IC3.2A
  N26: Part1.D23, IC3.1A
  N27: Part1.D24, IC3.3A
  N28: Part1.D25, IC3.4A
  N29: Part1.D42, MD03A2.2PWM
  N30: Part1.D43, MD03A2.2INb#143
  N31: Part1.D44, MD03A2.2INb#142
  N32: Part1.D46, J1.pulse
  N33: MD03A2.OUT_2A, DC_Mot_Enc10.pin1
  N34: MD03A2.OUT_2B, DC_Mot_Enc10.pin2
  N35: IC3.1Y, M1.B
  N36: IC3.2Y, M1.A
  N37: IC3.3Y, M1.C
  N38: IC3.4Y, M1.D
