# Fritzing sketch RobotProto (saved by Fritzing 0.9.3b)
breadboards: 1

parts:
  Part1 = Arduino Mega 2560 (Rev3)
  MD03A1 = Dual VNH2SP30 Motor Driver [part_number=MD03A]
  MD03A2 = Dual VNH2SP30 Motor Driver [part_number=MD03A]
  DC_Mot_Enc1 = DC Motor with two-phase hall-encoder [part_number=VT-E-G25A-06-177E]
  DC_Mot_Enc2 = DC Motor with two-phase hall-encoder [part_number=VT-E-G25A-06-177E]
  DC_Mot_Enc3 = DC Motor with two-phase hall-encoder [part_number=VT-E-G25A-06-177E]
  Part2 = NRF24L01+ Breakout Board
  DC_Mot_Enc4 = DC Motor with two-phase hall-encoder [part_number=VT-E-G25A-06-177E]
  DC_Mot_Enc5 = DC Motor with two-phase hall-encoder [part_number=VT-E-G25A-06-177E]
  VCC1 = 4 x AAA Battery Mount

nets:
  N1: Part1.D21/SCL, DC_Mot_Enc1.pin3
  N2: Part1.D20/SDA, DC_Mot_Enc1.pin6
  N3: Part1.D19/RX1, DC_Mot_Enc2.pin3
  N4: Part1.D18/TX1, DC_Mot_Enc2.pin6
  N5: Part1.D13_PWM, Part2.SCK
  N6: Part1.D12_PWM, Part2.MISO
  N7: Part1.D11_PWM, Part2.MOSI
  N8: Part1.D10_PWM, Part2.CS
  N9: Part1.D9_PWM, MD03A1.1INb
  N10: Part1.D8_PWM, Part2.CE
  3V3: Part1.3V3, Part2.VCC
  N11: Part1.5V, MD03A1.+5V_(IN), MD03A2.+5V_(IN), DC_Mot_Enc1.pin5, DC_Mot_Enc2.pin5
  GND: Part1.GND, MD03A1.GND#136, MD03A1.GND#138, MD03A2.GND#136, MD03A2.GND#138, DC_Mot_Enc1.pin4, DC_Mot_Enc2.pin4, Part2.GND
  N12: Part1.D3_PWM, MD03A1.PWM
  N13: Part1.D4_PWM, MD03A1.2PWM
  N14: Part1.D5_PWM, MD03A1.2INb#142
  N15: Part1.D6_PWM, MD03A1.2INb#143
  N16: Part1.D7_PWM, MD03A1.1INa
  N17: Part1.D47, MD03A2.2PWM
  N18: Part1.D48, MD03A2.2INb#143
  N19: Part1.D49, MD03A2.2INb#142
  N20: Part1.D51, MD03A2.PWM
  N21: Part1.D52, MD03A2.1INa
  N22: Part1.D53, MD03A2.1INb
  N23: MD03A1.OUT_1A, DC_Mot_Enc2.pin1, DC_Mot_Enc3.pin1
  N24: MD03A1.OUT_1B, DC_Mot_Enc2.pin2, DC_Mot_Enc3.pin2
  N25: MD03A1.OUT_2A, DC_Mot_Enc1.pin1, DC_Mot_Enc4.pin1
  N26: MD03A1.OUT_2B, DC_Mot_Enc1.pin2, DC_Mot_Enc4.pin2
  VIN: MD03A1.VIN, MD03A2.VIN, VCC1.+
  N27: MD03A1.GND#151, MD03A2.GND#151, VCC1.-
  N28: MD03A2.OUT_1A, DC_Mot_Enc5.pin1
  N29: MD03A2.OUT_1B, DC_Mot_Enc5.pin2
