# Fritzing sketch newstepper (saved by Fritzing 0.9.3b)
circuit board: 5.30155cm x 5.34835cm
breadboards: 1

parts:
  IC1 = H-Bridge [package=THT]
  IC2 = H-Bridge [package=THT]
  Part1 = Arduino Uno (Rev3) - ICSP
  M1 = Stepper Motor - Bipolar
  M2 = Stepper Motor - Bipolar
  VCC1 = Battery block 9V
  VCC2 = Battery block 9V

nets:
  N1: IC1.1_2EN, IC1.3_4EN, IC1.VCC1, IC2.1_2EN, IC2.3_4EN, IC2.VCC1, Part1.5V
  N2: IC1.1A, Part1.D5_PWM
  N3: IC1.1Y, M2.B
  GND1: IC1.GND1, IC1.GND2, IC1.GND3, IC1.GND4, IC2.GND1, IC2.GND2, IC2.GND3, IC2.GND4, Part1.GND, VCC1.-, VCC2.-
  N4: IC1.2Y, M2.A
  N5: IC1.2A, Part1.D4
  N6: IC1.VCC2, VCC2.+
  N7: IC1.3A, Part1.D6_PWM
  N8: IC1.3Y, M2.C
  N9: IC1.4Y, M2.D
  N10: IC1.4A, Part1.D7
  N11: IC2.1A, Part1.D9_PWM
  N12: IC2.1Y, M1.B
  N13: IC2.2Y, M1.A
  N14: IC2.2A, Part1.D8
  N15: IC2.VCC2, VCC1.+
  N16: IC2.3A, Part1.D10_PWM/SS
  N17: IC2.3Y, M1.C
  N18: IC2.4Y, M1.D
  N19: IC2.4A, Part1.D11_PWM/MOSI
